// Logisim project Latches, Stuff.circ as structural Verilog
module D_Latch (
  input  CLK,
  input  D,
  output Q,
  output Q_Comp
);

  wire and_1_out, and_2_out, not_1_out;

  not not_1 (not_1_out, D);
  and and_1 (and_1_out, CLK, not_1_out);
  and and_2 (and_2_out, CLK, D);
  SR_Latch sr_latch_1 (.R(and_1_out), .S(and_2_out), .Q(Q), .Q_Comp(Q_Comp));
endmodule

module SR_Latch (
  input  R,
  input  S,
  output Q,
  output Q_Comp
);

  nor nor_1 (Q, R, Q_Comp);
  nor nor_2 (Q_Comp, Q, S);
endmodule

module D_Flip_Flop (
  input  CLK,
  input  D,
  output Q,
  output Q_Comp
);

  wire d_latch_1_q, not_1_out;

  D_Latch d_latch_1 (.CLK(not_1_out), .D(D), .Q(d_latch_1_q));  // open: Q_Comp
  not not_1 (not_1_out, CLK);
  D_Latch d_latch_2 (.CLK(CLK), .D(d_latch_1_q), .Q(Q), .Q_Comp(Q_Comp));

  // Notes on the sheet:
  //   N1
endmodule

module _2_bit_Register (
  input  CLK,
  input  D1,
  input  D0,
  output Q1,
  output Q0
);

  D_Flip_Flop d_flip_flop_1 (.D(D1), .Q(Q1), .CLK(CLK));  // open: Q_Comp
  D_Flip_Flop d_flip_flop_2 (.D(D0), .Q(Q0), .CLK(CLK));  // open: Q_Comp
endmodule
