// Logisim project aluCirc.circ as structural Verilog: 1 circuit, main circuit main
module main (
  input  in_1,
  input  [1:0] SR1,
  input  [1:0] SR2,
  input  [1:0] in_4,
  input  [1:0] Operation,
  input  in_6,
  output [7:0] out_7
);

  wire and_1_out, and_2_out, and_3_out, and_4_out, decoder_1_out0, decoder_1_out1, decoder_1_out2,
       decoder_1_out3;
  wire [7:0] adder_1_out, multiplexer_1_out, multiplexer_3_out, multiplier_1_out, negator_1_out,
       register_1_q, register_2_q, register_3_q, register_4_q, register_5_q, subtractor_1_out;

  Decoder #(.select(2), .enable("false")) decoder_1 (
    .out0(decoder_1_out0), .out1(decoder_1_out1), .out2(decoder_1_out2), .out3(decoder_1_out3), .sel(in_4));
  and and_1 (and_1_out, in_1, decoder_1_out0);
  and and_2 (and_2_out, in_1, decoder_1_out1);
  and and_3 (and_3_out, in_1, decoder_1_out2);
  and and_4 (and_4_out, in_1, decoder_1_out3);
  Register register_1 (.D(register_5_q), .Q(register_1_q), .clk(and_1_out));  // open: en, clr
  Adder adder_1 (.a(multiplexer_1_out), .b(multiplexer_3_out), .out(adder_1_out));  // open: cin, cout
  Register register_2 (.D(register_5_q), .Q(register_2_q), .clk(and_2_out));  // open: en, clr
  Multiplexer #(.select(2), .width(8), .enable("false")) multiplexer_1 (
    .in0(register_1_q), .in1(register_2_q), .in2(register_3_q), .in3(register_4_q), .out(multiplexer_1_out),
    .sel(SR1));
  Subtractor subtractor_1 (.a(multiplexer_1_out), .b(multiplexer_3_out), .out(subtractor_1_out));  // open: bin, bout
  Multiplexer #(.select(2), .width(8), .enable("false")) multiplexer_2 (
    .in0(adder_1_out), .in1(subtractor_1_out), .in2(multiplier_1_out), .in3(negator_1_out), .out(out_7),
    .sel(Operation));
  Register register_3 (.D(register_5_q), .Q(register_3_q), .clk(and_3_out));  // open: en, clr
  Multiplexer #(.select(2), .width(8), .enable("false")) multiplexer_3 (
    .in0(register_1_q), .in1(register_2_q), .in2(register_3_q), .in3(register_4_q), .out(multiplexer_3_out),
    .sel(SR2));
  Register register_4 (.D(register_5_q), .Q(register_4_q), .clk(and_4_out));  // open: en, clr
  Multiplier multiplier_1 (.a(multiplexer_1_out), .b(multiplexer_3_out), .out(multiplier_1_out));  // open: cin, cout
  Register register_5 (.D(out_7), .Q(register_5_q), .clk(in_6));  // open: en, clr
  Negator negator_1 (.in(multiplexer_1_out), .out(negator_1_out));

  // Notes on the sheet:
  //   Destination Reg DR
  //   Save Result in Registers
  //   A
  //   Capture Math Result
  //   B
  //   D
  //   C
endmodule
