// Logisim project lab 3 practice.circ as structural Verilog
module Half_Adder (
  input  A,
  input  B,
  output out_3,
  output out_4
);

  xor xor_1 (out_3, A, B);
  and and_1 (out_4, A, B);
endmodule

module Full_Adder (
  input  Cin,
  input  B,
  input  A,
  output out_4,
  output out_5
);

  wire AB_out, AC_out, BC_out, xor_1_out;

  xor xor_1 (xor_1_out, B, A);
  and BC (BC_out, Cin, B);
  and AC (AC_out, Cin, A);
  and AB (AB_out, B, A);
  xor xor_2 (out_4, Cin, xor_1_out);
  or or_1 (out_5, BC_out, AC_out, AB_out);
endmodule
