// Logisim project lab03.circ as structural Verilog: 3 circuits, main circuit main
module main (
  input  in_1,
  input  in_2,
  input  in_3,
  input  in_4,
  input  in_5,
  input  in_6,
  input  in_7,
  input  in_8,
  input  in_9,
  output out_10,
  output out_11,
  output out_12,
  output out_13
);

  wire full_adder_2_out_5, full_adder_3_out_5, full_adder_4_out_5, xor_1_out, xor_2_out, xor_3_out, xor_4_out;

  Full_Adder full_adder_1 (.Cin(full_adder_2_out_5), .B(xor_1_out), .A(in_6), .out_4(out_10));  // open: out_5
  Full_Adder full_adder_2 (
    .Cin(full_adder_3_out_5), .B(xor_3_out), .A(in_7), .out_4(out_11), .out_5(full_adder_2_out_5));
  Full_Adder full_adder_3 (
    .Cin(full_adder_4_out_5), .B(xor_2_out), .A(in_8), .out_4(out_12), .out_5(full_adder_3_out_5));
  xor xor_1 (xor_1_out, in_1, in_5);
  Full_Adder full_adder_4 (.Cin(in_5), .B(xor_4_out), .A(in_9), .out_4(out_13), .out_5(full_adder_4_out_5));
  xor xor_2 (xor_2_out, in_3, in_5);
  xor xor_3 (xor_3_out, in_2, in_5);
  xor xor_4 (xor_4_out, in_4, in_5);
endmodule

module Half_Adder (
  input  A,
  input  B,
  output S,
  output C
);

  xor xor_1 (S, A, B);
  and and_1 (C, A, B);
endmodule

module Full_Adder (
  input  Cin,
  input  B,
  input  A,
  output out_4,
  output out_5
);

  wire AB_out, AC_out, BC_out, xor_1_out;

  xor xor_1 (xor_1_out, B, A);
  and BC (BC_out, Cin, B);
  and AC (AC_out, Cin, A);
  and AB (AB_out, B, A);
  xor xor_2 (out_4, Cin, xor_1_out);
  or or_1 (out_5, BC_out, AC_out, AB_out);
endmodule
