// Logisim project lab04.circ as structural Verilog
module _1 (
  input  A,
  input  B,
  input  C,
  input  D,
  output out_5
);

  wire and_1_out, and_2_out;

  and and_1 (and_1_out, ~B, ~D);  // AND_Gate
  or or_1 (out_5, and_1_out, and_2_out);
  and and_2 (and_2_out, A, C, D);
endmodule

module _2 (
  input  a,
  input  b,
  input  c,
  input  d,
  output out_5
);

  wire and_1_out, and_2_out, and_3_out;

  and and_1 (and_1_out, ~a, ~d);  // AND_Gate
  and and_2 (and_2_out, ~b, ~c);  // AND_Gate
  and and_3 (and_3_out, a, b, c, d);
  or or_1 (out_5, and_1_out, and_2_out, and_3_out);
endmodule
