// Logisim project multiplexer 0926.circ as structural Verilog
module multiplexer (
  input  [3:0] in_1,
  input  in_2,
  input  [3:0] in_3,
  input  [1:0] in_4,
  input  [3:0] in_5,
  input  [3:0] in_6,
  input  [1:0] in_7,
  output [3:0] out_8,
  output [3:0] out_9,
  output [3:0] out_10
);

  Multiplexer #(.select(2), .width(4)) multiplexer_1 (
    .in0(in_1), .in1(in_3), .in2(in_5), .in3(in_6), .out(out_8), .sel(in_4));  // open: en
  Multiplexer #(.select(2), .width(4)) multiplexer_2 (
    .in0(in_1), .in1(in_3), .in2(in_5), .in3(in_6), .out(out_10), .sel(in_7));  // open: en
endmodule

module flip4 (
  input  [3:0] in_1,
  input  in_2,
  output [3:0] out_3
);

  xor xor_1 (out_3[3], in_1[3], in_2);
  xor xor_2 (out_3[2], in_1[2], in_2);
  xor xor_3 (out_3[1], in_1[1], in_2);
  xor xor_4 (out_3[0], in_1[0], in_2);
endmodule
